# Fritzing sketch wiring_drone (saved by Fritzing 0.9.10b)

parts:
  Mod1 = Amica NodeMCU DEVKIT 1.0
  Q1 = Basic FET N-Channel [package="DPak [SMD]"]
  M1 = DC Motor [voltage_(max)=6V voltage_(min)=3V]
  Q2 = Basic FET N-Channel [package="DPak [SMD]"]
  U1 = LIPO-1000mAh [package=lipo-1000]
  M2 = DC Motor [voltage_(max)=6V voltage_(min)=3V]
  M3 = DC Motor [voltage_(max)=6V voltage_(min)=3V]
  M4 = DC Motor [voltage_(max)=6V voltage_(min)=3V]
  Q3 = Basic FET N-Channel [package="DPak [SMD]"]
  Q4 = Basic FET N-Channel [package="DPak [SMD]"]
  R1 = Resistor [tolerance=±5% power=0.25 resistance=1k package=THT]
  R2 = Resistor [tolerance=±5% power=0.25 resistance=1k package=THT]
  R3 = Resistor [tolerance=±5% power=0.25 resistance=1k package=THT]
  R4 = Resistor [tolerance=±5% power=0.25 resistance=1k package=THT]
  Composant1 = InvenSense MPU6050

nets:
  N1: Mod1.pin1, Mod1.pin_10, Composant1.VCC
  N2: Mod1.pin2, Mod1.pin_9, Mod1.pin_29, Q1.source, Q2.source, Q3.source, Q4.source, R1.Pin_0, R2.Pin_0, R3.Pin_0, R4.Pin_0, Composant1.GND
  N3: Mod1.pin5, Q1.Gate, R1.Pin_1
  N4: Mod1.pin6, Q2.Gate, R2.Pin_1
  N5: Mod1.pin7, Q3.Gate, R3.Pin_1
  N6: Mod1.pin8, Q4.Gate, R4.Pin_1
  N7: Mod1.pin_13, Composant1.SDA
  N8: Mod1.pin_14, Composant1.SCL
  N9: Mod1.pin_30, M1.pin_1, U1.+
  N10: Q1.drain, M1.pin_2
  N11: Q2.drain, M2.pin_2
  N12: M3.pin_2, Q3.drain
  N13: M4.pin_2, Q4.drain
