# Fritzing sketch wiring_drone_esp32 (saved by Fritzing 0.9.10b)
circuit board: 17.6363cm x 11.6132cm

parts:
  Q1 = Basic FET N-Channel [package="DPak [SMD]"]
  M1 = DC Motor [voltage_(max)=6V voltage_(min)=3V]
  U1 = LIPO-1000mAh [package=lipo-1000]
  M2 = DC Motor [voltage_(max)=6V voltage_(min)=3V]
  M3 = DC Motor [voltage_(max)=6V voltage_(min)=3V]
  R1 = Resistor [tolerance=±5% power=0.25 resistance=1k package=THT]
  Composant1 = InvenSense MPU6050
  A1 = FireBeetle2-ESP32-S3
  Q2 = Basic FET N-Channel [package="DPak [SMD]"]
  R2 = Resistor [tolerance=±5% power=0.25 resistance=1k package=THT]
  Q3 = Basic FET N-Channel [package="DPak [SMD]"]
  R3 = Resistor [tolerance=±5% power=0.25 resistance=1k package=THT]
  Q4 = Basic FET N-Channel [package="DPak [SMD]"]
  R4 = Resistor [tolerance=±5% power=0.25 resistance=1k package=THT]
  M4 = DC Motor [voltage_(max)=6V voltage_(min)=3V]

nets (from the breadboard view):
  N1: Q1.Gate, R1.Pin_0, A1.pin_1
  N2: Q1.drain, M1.pin_2
  N3: Q1.source, U1.-, R1.Pin_1, Composant1.GND, A1.pin_16, A1.pin_28, Q2.source, R2.Pin_1, Q3.source, R3.Pin_1, Q4.source, R4.Pin_1
  N4: M1.pin_1, M2.pin_1, M3.pin_1, Composant1.VCC, A1.pin_26, M4.pin_1
  N5: U1.+, A1.pin_15
  N6: M2.pin_2, Q2.drain
  N7: M3.pin_2, Q3.drain
  N8: Composant1.SCL, A1.pin_33
  N9: Composant1.SDA, A1.pin_34
  N10: A1.pin_2, Q2.Gate, R2.Pin_0
  N11: A1.pin_3, Q3.Gate, R3.Pin_0
  N12: A1.pin_4, Q4.Gate, R4.Pin_0
  N13: Q4.drain, M4.pin_2

notes:
  red/blue CW
  black/white CCW

custom parts:
  FireBeetle2-ESP32-S3: FireBeetle 2 ESP32-S3 is a high-performance main-controller built around the ESP32-S3-WROOM-1-N16R8 module. ESP32-S3-WROOM-1-N16R8 comes with 16MB Flash and 8MB PSRAM for storing more data.
